// Logisim project s-mips.circ as structural Verilog
module S_MIPS_Board (
  input  DESHABILITAR_DISPATCHER,
  output halt
);

  wire button_1_out, CLK, CS, d_ff_1_q, LCLR, LoadRAM, LoadRAMOn, LW, R_R_W, R_W, ram_dispatcher_1_finished,
       RCS, Reset_out, RST, TTY_EN;
  wire [2:0] KDB;
  wire [3:0] LMask, Mask, ram_1_read_time, ram_1_write_time, RMask;
  wire [6:0] KDB_DATA, TTY_DATA;
  wire [15:0] Addr, LAddr, RAddr;
  wire [31:0] I0, I1, I2, I3, LData, ram_1_data_out_0, ram_1_data_out_1, ram_1_data_out_2, ram_1_data_out_3,
       RI0, RI1, RI2, RI3;

  TTY #(.rows(25), .cols(80)) tty_1 (.data(TTY_DATA), .clk(CLK), .we(TTY_EN), .clr(RST));
  not not_1 (LoadRAMOn, ram_dispatcher_1_finished);
  RAM_Dispatcher ram_dispatcher_1 (
    .WriteTime(ram_1_write_time), .Clock(CLK), .Data(LData), .Address(LAddr), .Mask(LMask),
    .Finished(ram_dispatcher_1_finished), .Write(LW), .CLR(LCLR));
  Keyboard #(.buflen(64)) keyboard_1 (.clk(CLK), .re(KDB[0]), .avail(KDB[2]), .data(KDB_DATA));  // open: clr
  RAM ram_1 (
    .Address(RAddr), .Data_Out_0(ram_1_data_out_0), .Data_Out_1(ram_1_data_out_1),
    .Data_Out_2(ram_1_data_out_2), .Data_Out_3(ram_1_data_out_3), .Data_In_0(RI0), .Data_In_1(RI1),
    .Data_In_2(RI2), .Data_In_3(RI3), .Mask(RMask), .nRead_Write(R_R_W), .Chip_Select(RCS),
    .Read_Time(ram_1_read_time), .Reset(button_1_out), .Write_Time(ram_1_write_time));
  Button button_1 (.out(button_1_out));
  D_Flip_Flop d_ff_1 (.clk(CLK), .D(1'b1), .Q(d_ff_1_q), .reset(Reset_out));  // open: Qn, preset, en
  Button Reset (.out(Reset_out));
  S_MIPS s_mips_1 (
    .Kbd_Enable(KDB[0]), .Address(Addr), .Kbd_Clear(KDB[1]), .Kbd_Available(KDB[2]), .RAM_In_0(I0),
    .Kbd_ASCII_Data(KDB_DATA), .RAM_In_1(I1), .TTY_Enable(TTY_EN), .RAM_In_2(I2), .RAM_In_3(I3),
    .TTY_ASCII_Data(TTY_DATA), .Reset(RST), .RAM_Out_0(ram_1_data_out_0), .Clock(CLK),
    .RAM_Out_1(ram_1_data_out_1), .Stop(halt), .RAM_Out_2(ram_1_data_out_2), .RAM_Out_3(ram_1_data_out_3),
    .Mask(Mask), .Read_Time(ram_1_read_time), .Write_Time(ram_1_write_time), .nRead_Write(R_W),
    .Chip_Select(CS));
  D_Flip_Flop d_ff_2 (.clk(CLK), .D(d_ff_1_q), .Qn(LCLR), .reset(Reset_out));  // open: Q, preset, en
  or or_1 (RST, LCLR, LoadRAM);
  Clock clock_1 (.out(CLK));
  Multiplexer #(.width(32), .enable("false")) multiplexer_1 (.in0(I0), .in1(LData), .out(RI0), .sel(LoadRAM));
  Multiplexer #(.width(32), .enable("false")) multiplexer_2 (.in0(I1), .in1(LData), .out(RI1), .sel(LoadRAM));
  Multiplexer #(.width(32), .enable("false")) multiplexer_3 (.in0(I2), .in1(LData), .out(RI2), .sel(LoadRAM));
  Multiplexer #(.width(32), .enable("false")) multiplexer_4 (.in0(I3), .in1(LData), .out(RI3), .sel(LoadRAM));
  and and_1 (LoadRAM, ~DESHABILITAR_DISPATCHER, LoadRAMOn);  // AND_Gate
  Multiplexer #(.width(16), .enable("false")) multiplexer_5 (.in0(Addr), .in1(LAddr), .out(RAddr), .sel(LoadRAM));
  Multiplexer #(.width(4), .enable("false")) multiplexer_6 (.in0(Mask), .in1(LMask), .out(RMask), .sel(LoadRAM));
  Multiplexer #(.enable("false")) multiplexer_7 (.in0(CS), .in1(LW), .out(RCS), .sel(LoadRAM));
  Multiplexer #(.enable("false")) multiplexer_8 (.in0(R_W), .in1(LW), .out(R_R_W), .sel(LoadRAM));

  // Notes on the sheet:
  //   NO MODIFICAR
  //   Keyboard
endmodule

module RAM_Dispatcher (
  input  [3:0] WriteTime,
  input  Clock,
  input  CLR,
  output [31:0] Data,
  output [15:0] Address,
  output [3:0] Mask,
  output Finished,
  output Write
);

  wire demultiplexer_2_out1, demultiplexer_3_out1, End, IDLE_q, IncAddr, Load, or_1_out, or_2_out, While_q,
       WriteEnd;
  wire [3:0] counter_1_q;
  wire [31:0] CurrentAddress_q;

  or or_1 (or_1_out, IncAddr, demultiplexer_3_out1, Finished);
  D_Flip_Flop IDLE (.clk(Clock), .D(or_1_out), .Q(IDLE_q), .preset(CLR));  // open: Qn, en, reset
  Demultiplexer #(.enable("false")) demultiplexer_1 (.out0(Load), .out1(Finished), .in(IDLE_q), .sel(End));
  or or_2 (or_2_out, Write, Load);
  Counter #(.width(32), .max('hffffffff)) CurrentAddress (
    .count(IncAddr), .Q({CurrentAddress_q[31:18], Address, CurrentAddress_q[1:0]}), .clk(Clock), .clr(CLR));  // open: load, D, carry
  Demultiplexer #(.enable("false")) demultiplexer_2 (
    .out0(Write), .out1(demultiplexer_2_out1), .in(While_q), .sel(WriteEnd));
  D_Flip_Flop While (.clk(Clock), .D(or_2_out), .Q(While_q), .reset(CLR));  // open: Qn, preset, en
  Decoder #(.select(2)) decoder_1 (
    .out0(Mask[0]), .out1(Mask[1]), .out2(Mask[2]), .out3(Mask[3]), .sel(CurrentAddress_q[1:0]));  // open: en
  Demultiplexer #(.enable("false")) demultiplexer_3 (
    .out0(IncAddr), .out1(demultiplexer_3_out1), .in(demultiplexer_2_out1), .sel(End));
  RAM_part #(.addrWidth(18), .dataWidth(32)) ram_1 (
    .addr({Address, CurrentAddress_q[1:0]}), .data(Data), .clk(Clock));  // open: sel, ld, clr
  Counter #(.width(4), .max('hf)) counter_1 (
    .load(Load), .D(WriteTime), .count(Write), .Q(counter_1_q), .clk(Clock));  // open: carry, clr
  Comparator #(.width(32)) comparator_1 (.a(Data), .b({32{1'b1}}), .eq(End));  // open: gt, lt
  Comparator #(.width(4)) comparator_2 (.a(4'b0000), .b(counter_1_q), .eq(WriteEnd));  // open: gt, lt

  // Other names for the same wires on the sheet: CLK = Clock; Count = Write; WT[3:0] = WriteTime
endmodule

module RAM (
  input  [15:0] Address,
  input  [31:0] Data_In_0,
  input  [31:0] Data_In_1,
  input  [31:0] Data_In_2,
  input  [31:0] Data_In_3,
  input  [3:0] Mask,
  input  nRead_Write,
  input  Chip_Select,
  input  Reset,
  output [31:0] Data_Out_0,
  output [31:0] Data_Out_1,
  output [31:0] Data_Out_2,
  output [31:0] Data_Out_3,
  output [3:0] Read_Time,
  output [3:0] Write_Time
);

  wire and_2_out, and_3_out, and_4_out, and_5_out, and_6_out, and_7_out, and_8_out, and_9_out, Changed, CLK,
       comparator_2_eq, comparator_3_eq, comparator_4_eq, comparator_5_eq, comparator_6_eq, Count,
       demultiplexer_3_out0, Idle, Idle_q, Load, Load0, Load1, nand_1_out, or_1_out, or_2_out, or_3_out,
       or_4_out, or_5_out, or_6_out, or_7_out, or_8_out, or_9_out, or_10_out, Proc_q, Update_Mem, Zero_Time;
  wire [3:0] counter_1_q, multiplexer_1_out, subtractor_1_out;
  wire [31:0] register_1_q, register_2_q, register_3_q, register_4_q, register_5_q;

  // Probe on 4'b0011
  // Probe on 4'b0010
  Multiplexer #(.width(4), .enable("false")) multiplexer_1 (
    .in0(4'b0011), .in1(4'b0010), .out(multiplexer_1_out), .sel(nRead_Write));
  or or_1 (or_1_out, Idle, Update_Mem);
  or or_2 (or_2_out, ~Chip_Select, Reset);  // OR_Gate
  Subtractor #(.width(4)) subtractor_1 (.a(multiplexer_1_out), .b(4'b0010), .out(subtractor_1_out));  // open: bin, bout
  D_Flip_Flop u_Idle (.clk(CLK), .D(or_1_out), .Q(Idle_q), .preset(or_2_out));  // open: Qn, en, reset
  Demultiplexer #(.enable("false")) demultiplexer_1 (.out0(Idle), .out1(Load0), .in(Idle_q), .sel(Changed));
  // Probe on counter_1_q
  Counter #(.width(4), .max('hf)) counter_1 (
    .load(Load), .D(subtractor_1_out), .count(Count), .Q(counter_1_q), .clk(CLK), .clr(or_3_out));  // open: carry
  or or_3 (or_3_out, ~Chip_Select, Reset);  // OR_Gate
  Comparator #(.width(4), .mode("unsigned")) comparator_1 (
    .a(4'b0000), .b(counter_1_q), .eq(Zero_Time));  // open: gt, lt
  or or_4 (or_4_out, Count, Load0, Load1);
  Register #(.width(32)) register_1 (.D(Data_In_0), .en(Chip_Select), .Q(register_1_q), .clk(CLK), .clr(or_5_out));
  or or_5 (or_5_out, ~Chip_Select, Reset);  // OR_Gate
  Register #(.width(32)) register_2 (.D(Data_In_1), .en(Chip_Select), .Q(register_2_q), .clk(CLK), .clr(or_6_out));
  or or_6 (or_6_out, ~Chip_Select, Reset);  // OR_Gate
  Register #(.width(32)) register_3 (.D(Data_In_2), .en(Chip_Select), .Q(register_3_q), .clk(CLK), .clr(or_7_out));
  or or_7 (or_7_out, ~Chip_Select, Reset);  // OR_Gate
  Register #(.width(32)) register_4 (.D(Data_In_3), .en(Chip_Select), .Q(register_4_q), .clk(CLK), .clr(or_8_out));
  or or_8 (or_8_out, ~Chip_Select, Reset);  // OR_Gate
  Register #(.width(32)) register_5 (
    .D({{11{1'b1}}, nRead_Write, Mask, Address}), .en(Chip_Select), .Q(register_5_q), .clk(CLK),
    .clr(or_9_out));
  or or_9 (or_9_out, ~Chip_Select, Reset);  // OR_Gate
  D_Flip_Flop Proc (.clk(CLK), .D(or_4_out), .Q(Proc_q), .reset(or_10_out));  // open: Qn, preset, en
  or or_10 (or_10_out, ~Chip_Select, Reset);  // OR_Gate
  Demultiplexer #(.enable("false")) demultiplexer_2 (
    .out0(Count), .out1(Update_Mem), .in(demultiplexer_3_out0), .sel(Zero_Time));
  Demultiplexer #(.enable("false")) demultiplexer_3 (
    .out0(demultiplexer_3_out0), .out1(Load1), .in(Proc_q), .sel(Changed));
  Clock clock_1 (.out(CLK));
  Comparator #(.width(32)) comparator_2 (.a(register_1_q), .b(Data_In_0), .eq(comparator_2_eq));  // open: gt, lt
  Comparator #(.width(32)) comparator_3 (.a(register_2_q), .b(Data_In_1), .eq(comparator_3_eq));  // open: gt, lt
  Comparator #(.width(32)) comparator_4 (.a(register_3_q), .b(Data_In_2), .eq(comparator_4_eq));  // open: gt, lt
  Comparator #(.width(32)) comparator_5 (.a(register_4_q), .b(Data_In_3), .eq(comparator_5_eq));  // open: gt, lt
  Comparator #(.width(32)) comparator_6 (
    .a(register_5_q), .b({{11{1'b1}}, nRead_Write, Mask, Address}), .eq(comparator_6_eq));  // open: gt, lt
  nand nand_1 (nand_1_out, comparator_6_eq, comparator_2_eq, comparator_3_eq, comparator_4_eq, comparator_5_eq);
  and and_1 (Changed, nand_1_out, Chip_Select);
  or or_11 (Load, Count, Load1, Load0);
  and and_2 (and_2_out, Mask[0], Update_Mem, nRead_Write);
  and and_3 (and_3_out, Mask[1], Update_Mem, nRead_Write);
  and and_4 (and_4_out, Mask[2], Update_Mem, nRead_Write);
  and and_5 (and_5_out, Mask[3], Update_Mem, nRead_Write);
  RAM_part #(.addrWidth(16), .dataWidth(32), .bus("separate")) ram_1 (
    .addr(Address), .din(Data_In_0), .data(Data_Out_0), .str(and_2_out), .sel(Chip_Select), .clk(CLK),
    .ld(and_6_out), .clr(Reset));
  and and_6 (and_6_out, ~nRead_Write, Idle);  // AND_Gate
  RAM_part #(.addrWidth(16), .dataWidth(32), .bus("separate")) ram_2 (
    .addr(Address), .din(Data_In_1), .data(Data_Out_1), .str(and_3_out), .sel(Chip_Select), .clk(CLK),
    .ld(and_7_out), .clr(Reset));
  and and_7 (and_7_out, ~nRead_Write, Idle);  // AND_Gate
  RAM_part #(.addrWidth(16), .dataWidth(32), .bus("separate")) ram_3 (
    .addr(Address), .din(Data_In_2), .data(Data_Out_2), .str(and_4_out), .sel(Chip_Select), .clk(CLK),
    .ld(and_8_out), .clr(Reset));
  and and_8 (and_8_out, ~nRead_Write, Idle);  // AND_Gate
  RAM_part #(.addrWidth(16), .dataWidth(32), .bus("separate")) ram_4 (
    .addr(Address), .din(Data_In_3), .data(Data_Out_3), .str(and_5_out), .sel(Chip_Select), .clk(CLK),
    .ld(and_9_out), .clr(Reset));
  and and_9 (and_9_out, ~nRead_Write, Idle);  // AND_Gate

  assign Read_Time = 4'b0011;
  assign Write_Time = 4'b0010;

  // Other names for the same wires on the sheet: M0 = Mask[0]; M1 = Mask[1]; M2 = Mask[2]; M3 = Mask[3];
  //   RW = nRead_Write; CLR = Reset; CS = Chip_Select; Load2 = Count

  // Notes on the sheet:
  //   NO MODIFICAR
  //   excepto quizás los valores RT y WT
  //   BANK0
  //   BANK1
  //   BANK2
  //   BANK3
endmodule

module S_MIPS (
  input  Kbd_Available,
  input  [6:0] Kbd_ASCII_Data,
  input  [31:0] RAM_Out_0,
  input  [31:0] RAM_Out_1,
  input  Reset,
  input  [31:0] RAM_Out_2,
  input  Clock,
  input  [31:0] RAM_Out_3,
  input  [3:0] Read_Time,
  input  [3:0] Write_Time,
  output Kbd_Enable,
  output [15:0] Address,
  output Kbd_Clear,
  output TTY_Enable,
  output [6:0] TTY_ASCII_Data,
  output Stop,
  output [31:0] RAM_In_0,
  output [31:0] RAM_In_1,
  output [31:0] RAM_In_2,
  output [31:0] RAM_In_3,
  output [3:0] Mask,
  output nRead_Write,
  output Chip_Select
);

  wire control_unit_1_dasel, control_unit_1_dosel, control_unit_1_hl, control_unit_1_ldpc,
       control_unit_1_operandasel, control_unit_1_output_2, control_unit_1_wrf, control_unit_1_wsp, RamReady,
       UseRam, WriteRam;
  wire [1:0] Bank, control_unit_1_addrsel, control_unit_1_bcsel, control_unit_1_operandbsel;
  wire [2:0] control_unit_1_alusel, control_unit_1_disel, control_unit_1_flagssel;
  wire [5:0] FuncCode, OpCode;
  wire [31:0] AddrToRam, DataFromRam, le_mode_1_output, ToRam;

  Control_Unit_2 control_unit_1 (
    .in_1(OpCode), .in_2(FuncCode), .in_3(Clock), .in_4(Reset), .in_5(RamReady), .Halt(Stop),
    .AluSel(control_unit_1_alusel), .OperandASel(control_unit_1_operandasel),
    .OperandBSel(control_unit_1_operandbsel), .AddrSel(control_unit_1_addrsel), .Wsp(control_unit_1_wsp),
    .LdPc(control_unit_1_ldpc), .BcSel(control_unit_1_bcsel), .DiSel(control_unit_1_disel),
    .DoSel(control_unit_1_dosel), .FlagsSel(control_unit_1_flagssel), .DaSel(control_unit_1_dasel),
    .HL(control_unit_1_hl), .EnKbd(Kbd_Enable), .Output(TTY_Enable), .StartRam(UseRam),
    .Wrf(control_unit_1_wrf), .WRam(WriteRam), .Output_2(control_unit_1_output_2));
  Ram_Handler ram_handler_1 (
    .in_1(AddrToRam), .in_3(RAM_Out_1), .in_4(RAM_Out_2), .in_5(RAM_Out_3), .in_6(Clock), .in_7(Reset),
    .Read_Time(Read_Time), .in_9(UseRam), .in_10(WriteRam), .Write_Time(Write_Time), .RamOut(DataFromRam),
    .Output(Mask), .ADDR(Address), .Ram_Ready(RamReady), .CS(Chip_Select), .Output_2(nRead_Write),
    .Bank(Bank), .in_2(RAM_Out_0));
  DataPath datapath_1 (
    .in_4(control_unit_1_alusel), .in_9(control_unit_1_hl), .in_15(Clock), .in_1(control_unit_1_wrf),
    .in_7(Reset), .in_5(DataFromRam), .in_12(control_unit_1_disel), .in_16(control_unit_1_bcsel),
    .in_17(control_unit_1_ldpc), .in_11(control_unit_1_flagssel), .in_2(control_unit_1_dasel),
    .in_8(control_unit_1_output_2), .in_3(control_unit_1_addrsel), .in_6(control_unit_1_dosel),
    .in_10(control_unit_1_wsp), .in_14(control_unit_1_operandasel), .in_19(control_unit_1_operandbsel),
    .Address(AddrToRam), .Fun_Code(FuncCode), .Op(OpCode), .Data(ToRam), .Tty(TTY_ASCII_Data),
    .in_13(Kbd_Available), .in_18(Kbd_ASCII_Data));  // open: KBDData
  LE_Mode le_mode_1 (.in_1(ToRam), .Output(le_mode_1_output));
  Demultiplexer #(.select(2), .width(32), .enable("false")) demultiplexer_1 (
    .out0(RAM_In_0), .out1(RAM_In_1), .out2(RAM_In_2), .out3(RAM_In_3), .in(le_mode_1_output), .sel(Bank));

  assign Kbd_Clear = Reset;

  // Other names for the same wires on the sheet: CLK = Clock; CS = Chip_Select; Halt = Stop;
  //   KBD_AVAIL = Kbd_Available; CLR = Reset; KBD_CLR = Reset; KBD_DATA[6:0] = Kbd_ASCII_Data; RAM_A[15:0] = Address;
  //   RAM_INPUT_0[31:0] = RAM_In_0; RAM_INPUT_1[31:0] = RAM_In_1; RAM_INPUT_2[31:0] = RAM_In_2;
  //   RAM_INPUT_3[31:0] = RAM_In_3; RAM_MASK[3:0] = Mask; RAM_OUTPUT_0[31:0] = RAM_Out_0;
  //   RAM_OUTPUT_1[31:0] = RAM_Out_1; RAM_OUTPUT_2[31:0] = RAM_Out_2; RAM_OUTPUT_3[31:0] = RAM_Out_3;
  //   RW = nRead_Write; TTY_DATA[6:0] = TTY_ASCII_Data

  // Notes on the sheet:
  //   RAM ADDRESS
  //   DATA FROM RAM
  //   DATA TO RAM
  //   DATA WRITE MASK
  //   RAM TIMING
  //   RAM CONTROL
  //   KEYBOARD
  //   TTY
  //   SEQUENCING
endmodule

module Ram_Handler (
  input  [31:0] in_1,
  input  [31:0] in_2,
  input  [31:0] in_3,
  input  [31:0] in_4,
  input  [31:0] in_5,
  input  in_6,
  input  in_7,
  input  [3:0] Read_Time,
  input  in_9,
  input  in_10,
  input  [3:0] Write_Time,
  output [31:0] RamOut,
  output [3:0] Output,
  output [15:0] ADDR,
  output Ram_Ready,
  output CS,
  output Output_2,
  output [1:0] Bank
);

  wire Clear, comparator_1_lt, d_ff_1_q, demultiplexer_1_out0, IsFetch, or_1_out;
  wire [3:0] counter_1_q, Time;
  wire [31:0] multiplexer_2_out;

  Multiplexer #(.width(4), .enable("false")) multiplexer_1 (.in0(Read_Time), .in1(Write_Time), .out(Time), .sel(in_10));
  Counter #(.width(4), .max('hf)) counter_1 (
    .count(CS), .Q(counter_1_q), .clk(in_6), .clr(or_1_out));  // open: load, D, carry
  or or_1 (or_1_out, in_7, Clear);
  D_Flip_Flop d_ff_1 (.clk(in_6), .D(demultiplexer_1_out0), .Q(d_ff_1_q));  // open: Qn, preset, en, reset
  or or_2 (CS, d_ff_1_q, in_9);
  Comparator #(.width(4)) comparator_1 (.a(counter_1_q), .b(Time), .lt(comparator_1_lt));  // open: gt, eq
  not not_1 (IsFetch, comparator_1_lt);
  Demultiplexer #(.enable("false")) demultiplexer_1 (
    .out0(demultiplexer_1_out0), .out1(Ram_Ready), .in(CS), .sel(IsFetch));
  D_Flip_Flop d_ff_2 (.clk(in_6), .D(Ram_Ready), .Q(Clear));  // open: Qn, preset, en, reset
  Decoder #(.select(2), .enable("false")) decoder_1 (
    .out0(Output[0]), .out1(Output[1]), .out2(Output[2]), .out3(Output[3]), .sel(in_1[3:2]));
  LE_Mode le_mode_1 (.in_1(multiplexer_2_out), .Output(RamOut));
  Multiplexer #(.select(2), .width(32), .enable("false")) multiplexer_2 (
    .in0(in_2), .in1(in_3), .in2(in_4), .in3(in_5), .out(multiplexer_2_out), .sel(in_1[3:2]));
  and and_1 (Output_2, in_10, CS);

  assign ADDR = in_1[19:4];
  assign Bank = in_1[3:2];

  // Other names for the same wires on the sheet: Clk = in_6; End = Ram_Ready; Block[15:0] = in_1[19:4];
  //   RamOut0[31:0] = in_2; RamOut1[31:0] = in_3; RamOut2[31:0] = in_4; RamOut3[31:0] = in_5; Count = CS; RamWr = CS;
  //   Rst = in_7; Rw = in_10; Start = in_9

  // Notes on the sheet:
  //   Address
  //   Data From Ram
  //   Ram Timing
  //   Timer
  //   Flow Control
  //   Control Signals
endmodule

module LE_Mode (
  input  [31:0] in_1,
  output [31:0] Output
);


  assign Output = {in_1[7:0], in_1[15:8], in_1[23:16], in_1[31:24]};
endmodule

// End8
module Control_Unit_2 (
  input  [5:0] in_1,
  input  [5:0] in_2,
  input  in_3,
  input  in_4,
  input  in_5,
  output [2:0] AluSel,
  output LdPc,
  output OperandASel,
  output DaSel,
  output [1:0] BcSel,
  output [1:0] OperandBSel,
  output DoSel,
  output [2:0] FlagsSel,
  output HL,
  output [2:0] DiSel,
  output EnKbd,
  output [1:0] AddrSel,
  output Output,
  output Wrf,
  output Wsp,
  output Output_2,
  output WRam,
  output StartRam,
  output Halt
);

  wire Add, Addi, And, Andi, Beq, Bgtz, Blez, Bltz, Bne, d_ff_1_q, DaSel2, DaSel8, demultiplexer_1_out0,
       demultiplexer_1_out1, demultiplexer_2_out0, Div, Divu, EnableAl, EnableBranch, EnableInm, EnableLWord,
       EnablePop, EnablePush, EnableSpecial, EnableSWord, End7, End8, EndStackPop, EndStackPush, EnRam4,
       EnRam5, EnRam7, EnRam8, Halt_t, IDLE_q, J, Jr, Kbd, LdPc1, LdPc2, LdPc3, LdPc4, LdPc5, LdPc6, LdPc7,
       LdPc8, Load_IM_q, Lw, Mul, Mulu, MvHi, MvLo, Next, Nop, Nor, not_1_out, OperandASel4, OperandASel5,
       Or, or_2_out, or_5_out, Ori, Pop, Push, Rnd, Slt, Slti, Sltiu, Sltu, StartRamF, Sub, Sw, Tty, TypeAl,
       TypeBranch, TypeInm, TypeSpecial, WRam5, WRam7, Wrf1, Wrf2, Wrf4, Wrf6, Wrf8, Wsp4, Wsp5, Xor, Xori;
  wire [1:0] AddrSel4, AddrSel5, AddrSel7, AddrSel8, BcSel1, BcSel3, OperandBSel2, OperandBSel4,
       OperandBSel5, OperandBSel7, OperandBSel8;
  wire [2:0] AluSel1, AluSel2, AluSel3, AluSel5, DiSel1, DiSel4, DiSel6, DiSel8;

  D_Flip_Flop IDLE (.clk(in_3), .D(demultiplexer_1_out0), .Q(IDLE_q), .preset(in_4));  // open: Qn, en, reset
  Type_Load_Word type_load_word_1 (
    .in_1(EnableLWord), .in_2(in_3), .in_3(in_5), .OperandBSelector(OperandBSel8), .EnRam(EnRam8),
    .Wrf(Wrf8), .LdPc(LdPc8), .End(End8), .DaSel(DaSel8), .DiSel(DiSel8), .AddrSel(AddrSel8));
  Demultiplexer #(.enable("false")) demultiplexer_1 (
    .out0(demultiplexer_1_out0), .out1(demultiplexer_1_out1), .in(IDLE_q), .sel(not_1_out));
  not not_1 (not_1_out, in_4);
  Instruction_Decoder_Memory instruction_decoder_memory_1 (
    .nop(Nop), .in_1(in_1), .add(Add), .sub(Sub), .in_2(in_2), .mult(Mul), .mulu(Mulu), .div(Div),
    .divu(Divu), .slt(Slt), .sltu(Sltu), .\and (And), .\or (Or), .\xor (Xor), .\nor (Nor), .pop(Pop),
    .push(Push), .mfhi(MvHi), .mflo(MvLo), .jr(Jr), .addi(Addi), .sltiu(Sltiu), .slti(Slti), .ori(Ori),
    .andi(Andi), .xori(Xori), .lw(Lw), .sw(Sw), .beq(Beq), .bne(Bne), .blez(Blez), .bgtz(Bgtz), .bltz(Bltz),
    .J(J), .halt(Halt_t), .tty(Tty), .rnd(Rnd), .kbd(Kbd));
  Type_AL type_al_1 (
    .in_1(Add), .in_2(Sub), .in_4(Mulu), .in_5(Div), .in_6(Divu), .in_7(And), .in_8(Or), .in_9(Nor),
    .in_10(Xor), .in_11(Slt), .in_12(Sltu), .in_16(EnableAl), .in_3(Mul), .AluSel(AluSel1), .RfRw(Wrf1),
    .Pc(LdPc1), .in_13(Jr), .in_14(MvHi), .in_15(MvLo), .BcSel(BcSel1), .HL(HL), .DiSel(DiSel1));
  or or_1 (StartRamF, Next, demultiplexer_1_out1);
  Demultiplexer #(.enable("false")) demultiplexer_2 (
    .out0(demultiplexer_2_out0), .out1(Output_2), .in(or_2_out), .sel(in_5));
  or or_2 (or_2_out, StartRamF, d_ff_1_q);
  D_Flip_Flop d_ff_1 (.clk(in_3), .D(demultiplexer_2_out0), .Q(d_ff_1_q));  // open: Qn, preset, en, reset
  D_Flip_Flop Load_IM (.clk(in_3), .D(Output_2), .Q(Load_IM_q));  // open: Qn, preset, en, reset
  and and_1 (EnablePop, Pop, Load_IM_q);
  and and_2 (EnablePush, Push, Load_IM_q);
  and and_3 (EnableLWord, Lw, Load_IM_q);
  and and_4 (EnableSpecial, TypeSpecial, Load_IM_q);
  and and_5 (EnableBranch, TypeBranch, Load_IM_q);
  and and_6 (EnableInm, TypeInm, Load_IM_q);
  and and_7 (EnableAl, TypeAl, Load_IM_q);
  and and_8 (EnableSWord, Sw, Load_IM_q);
  Type_Inmediate type_inmediate_1 (
    .in_1(Addi), .in_2(Andi), .in_3(Ori), .in_4(Xori), .in_5(Slti), .in_6(Sltiu), .in_7(EnableInm),
    .DaSel(DaSel2), .BSel(OperandBSel2), .Pc(LdPc2), .RwRf(Wrf2), .AluSel(AluSel2));
  Branch_Operations branch_operations_1 (
    .in_1(Beq), .in_2(Bne), .in_3(Blez), .in_4(Bgtz), .in_5(Bltz), .in_7(EnableBranch), .in_6(Nop),
    .FlagsSel(FlagsSel), .in_8(J), .BcSel(BcSel3), .AluSel(AluSel3), .Pc(LdPc3));
  or or_3 (Wsp, Wsp4, Wsp5);
  Push push_1 (
    .in_1(EnablePush), .in_3(in_3), .in_2(in_5), .ASel(OperandASel5), .BSel(OperandBSel5),
    .AddrSel(AddrSel5), .SpRw(Wsp5), .Pc(LdPc5), .AluSel(AluSel5), .StartRam(EnRam5),
    .EndStack(EndStackPush), .RamW(WRam5), .DoSel(DoSel));
  or or_4 (StartRam, EnRam4, EnRam5, EnRam7, EnRam8, StartRamF);
  or or_5 (or_5_out, Halt_t, Halt);
  or or_6 (OperandASel, OperandASel4, OperandASel5);
  Pop pop_1 (
    .in_1(in_5), .in_2(EnablePop), .in_3(in_3), .Wrf(Wrf4), .EndStack(EndStackPop), .ASel(OperandASel4),
    .BSel(OperandBSel4), .SpRw(Wsp4), .LdPc(LdPc4), .StartRam(EnRam4), .DiSel(DiSel4), .AddrSel(AddrSel4));
  D_Flip_Flop #(.trigger("high")) u_Halt (.clk(in_3), .D(or_5_out), .Q(Halt));  // open: Qn, preset, en, reset
  assign AluSel = AluSel1 | AluSel2 | AluSel3 | AluSel5;  // OR_Gate or_7, 3 bits wide
  assign OperandBSel = OperandBSel4 | OperandBSel5 | OperandBSel2 | OperandBSel7;  // OR_Gate or_8, 2 bits wide
  assign AddrSel = AddrSel4 | AddrSel5 | AddrSel7;  // OR_Gate or_9, 2 bits wide
  assign BcSel = BcSel1 | BcSel3;  // OR_Gate or_10, 2 bits wide
  assign DiSel = DiSel1 | DiSel4 | DiSel6 | DiSel8;  // OR_Gate or_11, 3 bits wide
  Type_Store_Word type_store_word_1 (
    .in_1(EnableSWord), .in_2(in_3), .in_3(in_5), .WriteRam(WRam7), .OperandBSelector(OperandBSel7),
    .EnRam(EnRam7), .LdPc(LdPc7), .End(End7), .AddrSel(AddrSel7));
  or or_12 (LdPc, LdPc1, LdPc2, LdPc3, LdPc4, LdPc5, LdPc6, LdPc7, LdPc8);
  or or_13 (WRam, WRam5, WRam7);
  Type_Special type_special_1 (
    .in_1(Tty), .in_2(Rnd), .in_3(Kbd), .in_4(EnableSpecial), .Rf(Wrf6), .DiSel(DiSel6), .EnableTty(Output),
    .EnableKbd(EnKbd), .Pc(LdPc6));
  or or_14 (DaSel, DaSel2, DaSel8);
  or or_15 (Wrf, Wrf1, Wrf2, Wrf4, Wrf6, Wrf8);
  or or_16 (TypeBranch, Bne, Beq, Blez, J, Bgtz, Nop, Bltz);
  or or_17 (TypeAl, Divu, Mulu, Div, Mul, Sub, Add, MvHi, Jr, MvLo, Or, Sltu, Xor, Slt, Nor, And);
  or or_18 (TypeInm, Addi, Andi, Ori, Xori, Slti, Sltiu);
  or or_19 (Next, EnablePop, EnableSWord, EnablePush, EnableAl, EnableInm, EnableSpecial, EnableBranch, EnableLWord);
  or or_20 (TypeSpecial, Rnd, Tty, Kbd);

  // Other names for the same wires on the sheet: Clk = in_3; DoSel5 = DoSel; EnTty = Output; FuncCode[5:0] = in_2;
  //   LdIr = Output_2; OpCode[5:0] = in_1; RamReady = in_5; Start = in_4; WHL = HL

  // Notes on the sheet:
  //   Instruction Decoder
  //   Fetch Cycle
  //   Inputs
  //   Outputs
endmodule

module DataPath (
  input  in_1,
  input  in_2,
  input  [1:0] in_3,
  input  [2:0] in_4,
  input  [31:0] in_5,
  input  in_6,
  input  in_7,
  input  in_8,
  input  in_9,
  input  in_10,
  input  [2:0] in_11,
  input  [2:0] in_12,
  input  in_13,
  input  in_14,
  input  in_15,
  input  [1:0] in_16,
  input  in_17,
  input  [6:0] in_18,
  input  [1:0] in_19,
  input  [6:0] KBDData,
  output [31:0] Data,
  output [31:0] Address,
  output [5:0] Fun_Code,
  output [6:0] Tty,
  output [5:0] Op
);

  wire Ef, Gf, Lf;
  wire [4:0] Da, Rd, Rs, Rt;
  wire [15:0] OffSet;
  wire [25:0] Destiny;
  wire [31:0] AluHI, AluLo, AluResult, B, bit_extender_3_out, branch_control_1_pc, Di, Hi, InmSign, InmZero,
       IR_q, Kbd, Lo, multiplexer_2_out, multiplexer_3_out, Pc, Random, Rnd, Sp;
  wire [31:7] A;

  InstructionReport instructionreport_1 (
    .in_1(IR_q), .Func(Fun_Code), .Jump(Destiny), .Rd(Rd), .Rt(Rt), .Rs(Rs), .Inmediate(OffSet), .OpCode(Op));  // open: Shamt
  Register #(.width(32), .trigger("falling")) IR (.D(in_5), .en(in_8), .Q(IR_q), .clk(in_15));  // open: clr
  Branch_Control branch_control_1 (
    .in_1(Destiny), .in_2(Pc), .in_3(in_16), .in_6(Lf), .in_8(OffSet), .in_9({A, Tty}), .in_7(in_11),
    .in_4(Ef), .in_5(Gf), .Pc(branch_control_1_pc));
  Register #(.width(32)) u_PC (.D(branch_control_1_pc), .en(in_17), .Q(Pc), .clk(in_15), .clr(in_7));
  Register_File register_file_1 (
    .A({A, Tty}), .Di(Di), .B(B), .Da(Da), .Rw(in_1), .Sa(Rs), .Whl(in_9), .IHi(AluHI), .Ilow(AluLo),
    .Clock(in_15), .Rst(in_7), .Hi(Hi), .Low(Lo), .Sp(Sp), .in_10(AluResult), .in_12(in_10), .Sb(Rt));
  Multiplexer #(.width(32), .enable("false")) multiplexer_1 (.in0({A, Tty}), .in1(B), .out(Data), .sel(in_6));
  Multiplexer #(.width(32), .enable("false")) multiplexer_2 (
    .in0({A, Tty}), .in1(Sp), .out(multiplexer_2_out), .sel(in_14));
  Multiplexer #(.select(2), .width(32), .enable("false")) multiplexer_3 (
    .in0(B), .in1(32'h4), .in2(InmZero), .in3(InmSign), .out(multiplexer_3_out), .sel(in_19));
  Multiplexer #(.select(2), .width(32), .enable("false")) multiplexer_4 (
    .in0(AluResult), .in1(Pc), .in2({A, Tty}), .in3(Sp), .out(Address), .sel(in_3));
  ALU alu_1 (
    .in_2(multiplexer_2_out), .in_3(multiplexer_3_out), .HighOut(AluHI), .LowOut(AluLo), .Gf(Gf), .Ef(Ef),
    .Lf(Lf), .in_1(in_4), .Output(AluResult));
  Multiplexer #(.width(5), .enable("false")) multiplexer_5 (.in0(Rd), .in1(Rt), .out(Da), .sel(in_2));
  Random #(.width(32)) random_1 (.clk(in_15), .out(Rnd));  // open: next, clr
  Random #(.width(32)) random_2 (.clk(in_15), .next(1'b1), .out(Random));  // open: clr
  assign InmZero = {{16{1'b0}}, OffSet};  // Bit_Extender bit_extender_1
  assign InmSign = {{16{OffSet[15]}}, OffSet};  // Bit_Extender bit_extender_2
  assign bit_extender_3_out = {{25{1'b0}}, KBDData};  // Bit_Extender bit_extender_3
  Multiplexer #(.select(3), .width(32), .enable("false")) multiplexer_6 (
    .in0(AluResult), .in1(Hi), .in2(Lo), .in3(in_5), .in4(Kbd), .in5(Rnd), .out(Di), .sel(in_12));  // open: in6, in7
  Multiplexer #(.width(32), .enable("false")) multiplexer_7 (
    .in0(bit_extender_3_out), .in1({32{1'b1}}), .out(Kbd), .sel(in_13));

  // Other names for the same wires on the sheet: A[6:0] = Tty; AddressSel[1:0] = in_3; BranchSel[2:0] = in_11;
  //   Clk = in_15; DaSel = in_2; DataFromRam[31:0] = in_5; DataSel = in_6; DiSelector[2:0] = in_12;
  //   Func[5:0] = Fun_Code; InstructionRegisterLd = in_8; KbdAvaliable = in_13; KbdData_t[6:0] = in_18; LdPc = in_17;
  //   LdSp = in_10; OperandSelectorA = in_14; OperandSelectorB[1:0] = in_19; OperationSelector[2:0] = in_4;
  //   PcSel[1:0] = in_16; RstRf = in_7; Wrf = in_1; WriteHiLo = in_9

  // Notes on the sheet:
  //   Instruction Report
  //   Inputs
  //   Branch Control And PC
  //   Register File
  //   Outputs
  //   Arithmetic Logic Unity
  //   Auxiliary Ops
endmodule

module Branch_Control (
  input  [25:0] in_1,
  input  [31:0] in_2,
  input  [1:0] in_3,
  input  in_4,
  input  in_5,
  input  in_6,
  input  [2:0] in_7,
  input  [15:0] in_8,
  input  [31:0] in_9,
  output [31:0] Pc
);

  wire Flag, not_1_out, not_2_out;
  wire [31:0] adder_1_out, adder_2_out, multiplexer_2_out, OfSet, shifter_1_out;

  assign OfSet = {{16{1'b0}}, in_8};  // Bit_Extender bit_extender_1
  not not_1 (not_1_out, in_4);
  not not_2 (not_2_out, in_5);
  Adder #(.width(32)) adder_1 (.a(in_2), .b(32'h4), .out(adder_1_out));  // open: cin, cout
  Shifter #(.width(32)) shifter_1 (.in(OfSet), .\dist (5'b00010), .out(shifter_1_out));
  Multiplexer #(.select(3), .enable("false")) multiplexer_1 (
    .in0(in_4), .in1(not_1_out), .in2(in_5), .in3(not_2_out), .in4(in_6), .out(Flag), .sel(in_7));  // open: in5, in6, in7
  Adder #(.width(32)) adder_2 (.a(adder_1_out), .b(shifter_1_out), .out(adder_2_out));  // open: cin, cout
  Multiplexer #(.width(32), .enable("false")) multiplexer_2 (
    .in0(adder_1_out), .in1(adder_2_out), .out(multiplexer_2_out), .sel(Flag));
  Multiplexer #(.select(2), .width(32), .enable("false")) multiplexer_3 (
    .in0(adder_1_out), .in1(multiplexer_2_out), .in2(in_9), .in3({in_2[31:28], in_1, 2'b00}), .out(Pc),
    .sel(in_3));

  // Other names for the same wires on the sheet: Destiny[25:0] = in_1; Pc_t[31:0] = in_2; AluEf = in_4; AluGf = in_5;
  //   AluLf = in_6; BranchSelector[2:0] = in_7; PcSelector[1:0] = in_3; Rs[31:0] = in_9
endmodule

module Register_File (
  input  [4:0] Da,
  input  [31:0] Di,
  input  Rw,
  input  [4:0] Sa,
  input  [31:0] IHi,
  input  [4:0] Sb,
  input  [31:0] Ilow,
  input  Whl,
  input  Clock,
  input  [31:0] in_10,
  input  Rst,
  input  in_12,
  output [31:0] A,
  output [31:0] B,
  output [31:0] Hi,
  output [31:0] Low,
  output [31:0] Sp
);

  wire Ld00, Ld01, Ld02, Ld03, Ld04, Ld05, Ld06, Ld07, Ld08, Ld09, Ld10, Ld11, Ld12, Ld13, Ld14, Ld15, Ld16,
       Ld17, Ld18, Ld19, Ld20, Ld21, Ld22, Ld23, Ld24, Ld25, Ld26, Ld27, Ld28, Ld29, Ld30;
  wire [31:0] R00, R01, R02, R03, R04, R05, R06, R07, R08, R09, R10, R11, R12, R13, R14, R15, R16, R17, R18,
       R19, R20, R21, R22, R23, R24, R25, R26, R27, R28, R29, R30, undriven, undriven_2;

  Demultiplexer #(.select(5), .disabled(0), .enable("false")) demultiplexer_1 (
    .out0(Ld00), .out1(Ld01), .out2(Ld02), .out3(Ld03), .out4(Ld04), .out5(Ld05), .out6(Ld06), .out7(Ld07),
    .out8(Ld08), .out9(Ld09), .out10(Ld10), .out11(Ld11), .out12(Ld12), .out13(Ld13), .out14(Ld14),
    .out15(Ld15), .out16(Ld16), .out17(Ld17), .out18(Ld18), .out19(Ld19), .out20(Ld20), .out21(Ld21),
    .out22(Ld22), .out23(Ld23), .out24(Ld24), .out25(Ld25), .out26(Ld26), .out27(Ld27), .out28(Ld28),
    .out29(Ld29), .out30(Ld30), .in(Rw), .sel(Da));  // open: out31
  Register #(.width(32), .trigger("falling")) RHi (.D(IHi), .en(Whl), .Q(Hi), .clk(Clock), .clr(Rst));
  Register #(.width(32), .trigger("falling")) Rlow (.D(Ilow), .en(Whl), .Q(Low), .clk(Clock), .clr(Rst));
  Register #(.width(32), .trigger("falling")) u_R00 (.D(Di), .en(Ld00), .Q(R00), .clk(Clock), .clr(Rst));
  Register #(.width(32), .trigger("falling")) u_R04 (.D(Di), .en(Ld04), .Q(R04), .clk(Clock), .clr(Rst));
  Register #(.width(32), .trigger("falling")) u_R08 (.D(Di), .en(Ld08), .Q(R08), .clk(Clock), .clr(Rst));
  Register #(.width(32), .trigger("falling")) u_R12 (.D(Di), .en(Ld12), .Q(R12), .clk(Clock), .clr(Rst));
  Register #(.width(32), .trigger("falling")) u_R16 (.D(Di), .en(Ld16), .Q(R16), .clk(Clock), .clr(Rst));
  Register #(.width(32), .trigger("falling")) u_R20 (.D(Di), .en(Ld20), .Q(R20), .clk(Clock), .clr(Rst));
  Register #(.width(32), .trigger("falling")) u_R24 (.D(Di), .en(Ld24), .Q(R24), .clk(Clock), .clr(Rst));
  Register #(.width(32), .trigger("falling")) u_R28 (.D(Di), .en(Ld28), .Q(R28), .clk(Clock), .clr(Rst));
  Register #(.width(32), .trigger("falling")) u_R01 (.D(Di), .en(Ld01), .Q(R01), .clk(Clock), .clr(Rst));
  Register #(.width(32), .trigger("falling")) u_R05 (.D(Di), .en(Ld05), .Q(R05), .clk(Clock), .clr(Rst));
  Register #(.width(32), .trigger("falling")) u_R09 (.D(Di), .en(Ld09), .Q(R09), .clk(Clock), .clr(Rst));
  Register #(.width(32), .trigger("falling")) u_R13 (.D(Di), .en(Ld13), .Q(R13), .clk(Clock), .clr(Rst));
  Register #(.width(32), .trigger("falling")) u_R17 (.D(Di), .en(Ld17), .Q(R17), .clk(Clock), .clr(Rst));
  Register #(.width(32), .trigger("falling")) u_R21 (.D(Di), .en(Ld21), .Q(R21), .clk(Clock), .clr(Rst));
  Register #(.width(32), .trigger("falling")) u_R25 (.D(Di), .en(Ld25), .Q(R25), .clk(Clock), .clr(Rst));
  Register #(.width(32), .trigger("falling")) u_R29 (.D(Di), .en(Ld29), .Q(R29), .clk(Clock), .clr(Rst));
  Register #(.width(32), .trigger("falling")) u_R02 (.D(Di), .en(Ld02), .Q(R02), .clk(Clock), .clr(Rst));
  Register #(.width(32), .trigger("falling")) u_R06 (.D(Di), .en(Ld06), .Q(R06), .clk(Clock), .clr(Rst));
  Register #(.width(32), .trigger("falling")) u_R10 (.D(Di), .en(Ld10), .Q(R10), .clk(Clock), .clr(Rst));
  Register #(.width(32), .trigger("falling")) u_R14 (.D(Di), .en(Ld14), .Q(R14), .clk(Clock), .clr(Rst));
  Register #(.width(32), .trigger("falling")) u_R18 (.D(Di), .en(Ld18), .Q(R18), .clk(Clock), .clr(Rst));
  Register #(.width(32), .trigger("falling")) u_R22 (.D(Di), .en(Ld22), .Q(R22), .clk(Clock), .clr(Rst));
  Register #(.width(32), .trigger("falling")) u_R26 (.D(Di), .en(Ld26), .Q(R26), .clk(Clock), .clr(Rst));
  Register #(.width(32), .trigger("falling")) u_R30 (.D(Di), .en(Ld30), .Q(R30), .clk(Clock), .clr(Rst));
  Register #(.width(32), .trigger("falling")) u_R03 (.D(Di), .en(Ld03), .Q(R03), .clk(Clock), .clr(Rst));
  Register #(.width(32), .trigger("falling")) u_R07 (.D(Di), .en(Ld07), .Q(R07), .clk(Clock), .clr(Rst));
  Register #(.width(32), .trigger("falling")) u_R11 (.D(Di), .en(Ld11), .Q(R11), .clk(Clock), .clr(Rst));
  Register #(.width(32), .trigger("falling")) u_R15 (.D(Di), .en(Ld15), .Q(R15), .clk(Clock), .clr(Rst));
  Register #(.width(32), .trigger("falling")) u_R19 (.D(Di), .en(Ld19), .Q(R19), .clk(Clock), .clr(Rst));
  Register #(.width(32), .trigger("falling")) u_R23 (.D(Di), .en(Ld23), .Q(R23), .clk(Clock), .clr(Rst));
  Register #(.width(32), .trigger("falling")) u_R27 (.D(Di), .en(Ld27), .Q(R27), .clk(Clock), .clr(Rst));
  Register #(.width(32), .trigger("falling")) R31 (.D(in_10), .en(in_12), .Q(Sp), .clk(Clock), .clr(Rst));
  Multiplexer #(.select(5), .width(32), .enable("false")) multiplexer_1 (
    .in0(R00), .in1(R01), .in2(R02), .in3(R03), .in4(R04), .in5(undriven), .in6(R06), .in7(R07), .in8(R08),
    .in9(R09), .in10(R10), .in11(R11), .in12(R12), .in13(R13), .in14(R14), .in15(R15), .in16(R16),
    .in17(R17), .in18(R18), .in19(R19), .in20(R20), .in21(R21), .in22(R22), .in23(R23), .in24(R24),
    .in25(R25), .in26(R26), .in27(R27), .in28(R28), .in29(R29), .in30(R30), .out(A), .sel(Sa));  // open: in31
  Multiplexer #(.select(5), .width(32), .enable("false")) multiplexer_2 (
    .in0(R00), .in1(R01), .in2(R02), .in3(R03), .in4(R04), .in5(undriven_2), .in6(R06), .in7(R07), .in8(R08),
    .in9(R09), .in10(R10), .in11(R11), .in12(R12), .in13(R13), .in14(R14), .in15(R15), .in16(R16),
    .in17(R17), .in18(R18), .in19(R19), .in20(R20), .in21(R21), .in22(R22), .in23(R23), .in24(R24),
    .in25(R25), .in26(R26), .in27(R27), .in28(R28), .in29(R29), .in30(R30), .out(B), .sel(Sb));  // open: in31

  // Other names for the same wires on the sheet: Clk = Clock; InSp[31:0] = in_10; LdSp = in_12; RHi[31:0] = Hi;
  //   RLow[31:0] = Low

  // Notes on the sheet:
  //   Sa: pull=down
  //   Inputs
  //   High-Low
  //   Register  0
  //   Register  4
  //   Register  8
  //   Register  12
  //   Register  16
  //   Register  20
  //   Register  24
  //   Register  28
  //   Register  1
  //   Register  5
  //   Register  9
  //   Register  13
  //   Register  17
  //   Register  21
  //   Register  25
  //   Register  29
  //   Registers
  //   Register  2
  //   Register  6
  //   Register  10
  //   Register  14
  //   Register  18
  //   Register  22
  //   Register  26
  //   Register  30
  //   Register  3
  //   Register  7
  //   Register  11
  //   Register  15
  //   Register  19
  //   Register  23
  //   Register  27
  //   Register  31
  //   Outputs
endmodule

module ALU (
  input  [2:0] in_1,
  input  [31:0] in_2,
  input  [31:0] in_3,
  output [31:0] HighOut,
  output [31:0] LowOut,
  output [31:0] Output,
  output Gf,
  output Ef,
  output Lf
);

  wire Addc, comparator_2_lt, Subc;
  wire [31:0] Add, And, DivHi, DivLo, DivuHi, DivuLo, MulLo, MuluHi, MuluLo, Nor, Or, Sit, Situ, Sub, Xor;

  assign And = in_2 & in_3;  // AND_Gate and_1, 32 bits wide
  assign Or = in_2 | in_3;  // OR_Gate or_1, 32 bits wide
  assign Nor = ~(in_2 | in_3);  // NOR_Gate nor_1, 32 bits wide
  assign Xor = in_2 ^ in_3;  // XOR_Gate xor_1, 32 bits wide
  Comparator #(.width(32), .mode("unsigned")) comparator_1 (.a(Output), .b({32{1'b0}}), .gt(Gf), .eq(Ef), .lt(Lf));
  // Mul_signed mul_signed_1: pin names not known; wires that end beside it: in_2, in_3, MulLo
  // Div_Signed div_signed_1: pin names not known; wires that end beside it: in_2, in_3, DivHi, DivLo
  Adder #(.width(32)) adder_1 (.a(in_2), .b(in_3), .out(Add), .cout(Addc));  // open: cin
  Subtractor #(.width(32)) subtractor_1 (.a(in_2), .b(in_3), .out(Sub), .bout(Subc));  // open: bin
  Multiplier #(.width(32)) multiplier_1 (.a(in_2), .b(in_3), .out(MuluLo), .cout(MuluHi));  // open: cin
  Divider #(.width(32)) divider_1 (.a(in_2), .b(in_3), .out(DivuLo), .rem(DivuHi));  // open: upper
  assign Situ = {{31{1'b0}}, Lf};  // Bit_Extender bit_extender_1
  Comparator #(.width(32)) comparator_2 (.a(in_2), .b(in_3), .lt(comparator_2_lt));  // open: gt, eq
  assign Sit = {{31{1'b0}}, comparator_2_lt};  // Bit_Extender bit_extender_2
  Multiplexer #(.select(2), .width(32), .enable("false")) multiplexer_1 (
    .in0(MuluLo), .in1(MulLo), .in2(DivuLo), .in3(DivLo), .out(HighOut), .sel(in_1[1:0]));
  Multiplexer #(.select(2), .width(32), .enable("false")) multiplexer_2 (
    .in0(MuluLo), .in1(MulLo), .in2(DivuLo), .in3(DivLo), .out(LowOut), .sel(in_1[1:0]));
  Multiplexer #(.select(3), .width(32), .enable("false")) multiplexer_3 (
    .in0(Add), .in1(Sub), .in2(And), .in3(Or), .in4(Nor), .in5(Xor), .in6(Sit), .in7(Situ), .out(Output),
    .sel(in_1));

  // Other names for the same wires on the sheet: A[31:0] = in_2; B[31:0] = in_3; Hio[31:0] = HighOut;
  //   Lwo[31:0] = LowOut; Result[31:0] = Output; LoHiS[1:0] = in_1[1:0]; S[2:0] = in_1; SelectGeneral[2:0] = in_1

  // Notes on the sheet:
  //   Imputs
  //   Logic Operations
  //   Arithmetic Logic Unity
  //   Arithmetic Operations
  //   Comparison Operations
endmodule

module Div_Signed (
  input  [31:0] x,
  input  [31:0] y,
  output [31:0] DivRem,
  output [31:0] Div
);

  wire SignX, SignY, xor_1_out;
  wire [31:0] adder_1_out, Div_t, multiplexer_4_out, negator_1_out, negator_2_out, negator_3_out, Rem,
       subtractor_1_out, X1, Y1;

  Subtractor #(.width(32)) subtractor_1 (.a(Y1), .b(Rem), .out(subtractor_1_out));  // open: bin, bout
  Multiplexer #(.width(32)) multiplexer_1 (.in0(Rem), .in1(subtractor_1_out), .out(DivRem), .sel(SignX));  // open: en
  Sign_Getter sign_getter_1 (.in_1(x), .Output(SignX));
  Sign_Getter sign_getter_2 (.in_1(y), .Output(SignY));
  Negator #(.width(32)) negator_1 (.in(x), .out(negator_1_out));
  Negator #(.width(32)) negator_2 (.in(y), .out(negator_2_out));
  Multiplexer #(.width(32), .enable("false")) multiplexer_2 (.in0(x), .in1(negator_1_out), .out(X1), .sel(SignX));
  Multiplexer #(.width(32), .enable("false")) multiplexer_3 (.in0(y), .in1(negator_2_out), .out(Y1), .sel(SignY));
  Divider #(.width(32)) divider_1 (.a(X1), .b(Y1), .out(Div_t), .rem(Rem));  // open: upper
  Adder #(.width(32)) adder_1 (.a(Div_t), .b(32'h1), .out(adder_1_out));  // open: cin, cout
  Multiplexer #(.width(32), .enable("false")) multiplexer_4 (
    .in0(Div_t), .in1(adder_1_out), .out(multiplexer_4_out), .sel(SignX));
  Negator #(.width(32)) negator_3 (.in(multiplexer_4_out), .out(negator_3_out));
  Multiplexer #(.width(32), .enable("false")) multiplexer_5 (
    .in0(multiplexer_4_out), .in1(negator_3_out), .out(Div), .sel(xor_1_out));
  xor xor_1 (xor_1_out, SignY, SignX);

  // Other names for the same wires on the sheet: OH[31:0] = DivRem; OL[31:0] = Div
endmodule

module Mul_signed (
  input  [31:0] In1,
  input  [31:0] In2,
  output [31:0] Lo,
  output [31:0] Hi
);

  wire adder_1_cout, adder_3_cout;
  wire [15:0] mix1_high, mix1_low, mix2_high, mix2_low;
  wire [31:0] adder_1_out, adder_2_out, bit_extender_1_out, bit_extender_2_out, prehigh, prelower, value_1_0,
       value_1_1, value_2_0, value_2_1;

  assign bit_extender_1_out = {{16{1'b0}}, mix1_high};  // Bit_Extender bit_extender_1
  assign bit_extender_2_out = {{16{1'b0}}, mix2_high};  // Bit_Extender bit_extender_2
  assign value_1_0 = {{16{1'b0}}, In1[15:0]};  // Bit_Extender bit_extender_3
  assign value_1_1 = {{16{1'b0}}, In1[31:16]};  // Bit_Extender bit_extender_4
  assign value_2_0 = {{16{1'b0}}, In2[15:0]};  // Bit_Extender bit_extender_5
  assign value_2_1 = {{16{1'b0}}, In2[31:16]};  // Bit_Extender bit_extender_6
  Adder #(.width(32)) adder_1 (
    .a({mix1_low, {16{1'b0}}}), .b({mix2_low, {16{1'b0}}}), .out(adder_1_out), .cout(adder_1_cout));  // open: cin
  Adder #(.width(32)) adder_2 (
    .a(bit_extender_1_out), .b(bit_extender_2_out), .out(adder_2_out), .cin(adder_1_cout));  // open: cout
  Adder #(.width(32)) adder_3 (.a(prelower), .b(adder_1_out), .out(Lo), .cout(adder_3_cout));  // open: cin
  Adder #(.width(32)) adder_4 (.a(prehigh), .b(adder_2_out), .out(Hi), .cin(adder_3_cout));  // open: cout
  Multiplier #(.width(32)) multiplier_1 (.a(value_1_0), .b(value_2_0), .out(prelower));  // open: cin, cout
  Multiplier #(.width(32)) multiplier_2 (.a(value_1_0), .b(value_2_1), .out({mix1_high, mix1_low}));  // open: cin, cout
  Multiplier #(.width(32)) multiplier_3 (.a(value_1_1), .b(value_2_0), .out({mix2_high, mix2_low}));  // open: cin, cout
  Multiplier #(.width(32)) multiplier_4 (.a(value_1_1), .b(value_2_1), .out(prehigh));  // open: cin, cout
endmodule

module Sign_Getter (
  input  [31:0] in_1,
  output Output
);


  assign Output = in_1[31];
endmodule

module Comparer (
  input  [31:0] in_1,
  input  [31:0] in_2,
  output [31:0] Out
);

  wire comparator_1_lt;

  Comparator #(.width(32)) comparator_1 (.a(in_1), .b(in_2), .lt(comparator_1_lt));  // open: gt, eq
  Multiplexer #(.width(32), .enable("false")) multiplexer_1 (
    .in0(32'h1), .in1({32{1'b0}}), .out(Out), .sel(comparator_1_lt));
endmodule

module ComparerUnsigned (
  input  [31:0] in_1,
  input  [31:0] in_2,
  output [31:0] Out
);

  wire comparator_1_lt;

  Comparator #(.width(32), .mode("unsigned")) comparator_1 (.a(in_1), .b(in_2), .lt(comparator_1_lt));  // open: gt, eq
  Multiplexer #(.width(32), .enable("false")) multiplexer_1 (
    .in0(32'h1), .in1({32{1'b0}}), .out(Out), .sel(comparator_1_lt));
endmodule

module ZeroFlag (
  input  [31:0] IN,
  output ZF
);

  nor nor_1 (ZF, IN[0], IN[1], IN[2], IN[3], IN[4], IN[5], IN[6], IN[7], IN[8], IN[9], IN[10], IN[11], IN[12], IN[13], IN[14], IN[15], IN[16], IN[17], IN[18], IN[19], IN[20], IN[21], IN[22], IN[23], IN[24], IN[25], IN[26], IN[27], IN[28], IN[29], IN[30], IN[31]);
endmodule

module InstructionReport (
  input  [31:0] in_1,
  output [5:0] Func,
  output [25:0] Jump,
  output [4:0] Shamt,
  output [4:0] Rd,
  output [4:0] Rt,
  output [4:0] Rs,
  output [15:0] Inmediate,
  output [5:0] OpCode
);


  assign Func = in_1[5:0];
  assign Inmediate = in_1[15:0];
  assign Jump = in_1[25:0];
  assign OpCode = in_1[31:26];
  assign Rd = in_1[15:11];
  assign Rs = in_1[25:21];
  assign Rt = in_1[20:16];
  assign Shamt = in_1[10:6];
endmodule

module Instruction_Decoder_Memory (
  input  [5:0] in_1,
  input  [5:0] in_2,
  output nop,
  output add,
  output sub,
  output mult,
  output mulu,
  output div,
  output divu,
  output slt,
  output sltu,
  output \and ,
  output \or ,
  output \xor ,
  output \nor ,
  output pop,
  output push,
  output mfhi,
  output mflo,
  output jr,
  output addi,
  output sltiu,
  output slti,
  output ori,
  output andi,
  output xori,
  output lw,
  output sw,
  output beq,
  output bne,
  output blez,
  output bgtz,
  output bltz,
  output J,
  output halt,
  output tty,
  output rnd,
  output kbd
);

  wire _00, _01, _10, _11, and_10_out, and_11_out, and_25_out, and_26_out, and_27_out, and_34_out,
       and_41_out, and_46_out, comparator_1_eq, Especial, I, or_1_out, R, R_00, R_01, R_10;

  and and_1 (_10, ~in_1[0], I, in_1[1]);  // AND_Gate
  and and_2 (_11, in_1[0], I, in_1[1]);
  and and_3 (_01, in_1[0], I, ~in_1[1]);  // AND_Gate
  and and_4 (_00, ~in_1[0], I, ~in_1[1]);  // AND_Gate
  and and_5 (addi, ~in_1[2], _00, in_1[3]);  // AND_Gate
  and and_6 (andi, in_1[2], _00, in_1[3]);
  and and_7 (beq, in_1[2], _00, ~in_1[3]);  // AND_Gate
  and and_8 (mflo, ~in_2[3], R_01, in_2[1]);  // AND_Gate
  and and_9 (mfhi, ~in_2[3], R_01, ~in_2[1]);  // AND_Gate
  and and_10 (and_10_out, in_2[3], R_01, ~in_2[1]);  // AND_Gate
  and and_11 (and_11_out, in_2[3], R_01, in_2[1]);
  and and_12 (mulu, and_10_out, in_2[0]);
  and and_13 (divu, and_11_out, in_2[0]);
  and and_14 (div, and_11_out, ~in_2[0]);  // AND_Gate
  and and_15 (mult, and_10_out, ~in_2[0]);  // AND_Gate
  and and_16 (slti, ~in_1[2], _10, in_1[3]);  // AND_Gate
  and and_17 (xori, in_1[2], _10, in_1[3]);
  and and_18 (blez, in_1[2], _10, ~in_1[3]);  // AND_Gate
  and and_19 (R_00, ~in_2[4], R, ~in_2[5]);  // AND_Gate
  and and_20 (R_10, ~in_2[4], R, in_2[5]);  // AND_Gate
  and and_21 (R_01, in_2[4], R, ~in_2[5]);  // AND_Gate
  and and_22 (bne, in_1[2], _01, ~in_1[3]);  // AND_Gate
  and and_23 (ori, in_1[2], _01, in_1[3]);
  and and_24 (bltz, ~in_1[2], _01, ~in_1[3]);  // AND_Gate
  and and_25 (and_25_out, ~in_2[3], R_10, ~in_2[2]);  // AND_Gate
  and and_26 (and_26_out, in_2[3], R_10, in_2[1]);
  and and_27 (and_27_out, ~in_2[3], R_10, in_2[2]);  // AND_Gate
  and and_28 (\xor , in_2[3], R_10, ~in_2[1]);  // AND_Gate
  and and_29 (sub, in_2[1], and_25_out);
  and and_30 (add, ~in_2[1], and_25_out);  // AND_Gate
  and and_31 (sltu, and_26_out, in_2[0]);
  and and_32 (slt, ~in_2[0], and_26_out);  // AND_Gate
  and and_33 (\and , and_27_out, ~in_2[0]);  // AND_Gate
  and and_34 (and_34_out, and_27_out, in_2[0]);
  and and_35 (\nor , and_34_out, in_2[1]);
  and and_36 (\or , ~in_2[1], and_34_out);  // AND_Gate
  and and_37 (sltiu, ~in_1[5], _11, in_1[3]);  // AND_Gate
  and and_38 (sw, in_1[5], _11, in_1[3]);
  and and_39 (lw, in_1[5], _11, ~in_1[3]);  // AND_Gate
  and and_40 (bgtz, ~in_1[5], _11, ~in_1[3]);  // AND_Gate
  Comparator #(.width(6)) comparator_1 (.a(in_1), .b({6{1'b0}}), .eq(comparator_1_eq));  // open: gt, lt
  or or_1 (or_1_out, comparator_1_eq, and_41_out);
  and and_41 (and_41_out, in_1[5], in_1[4], in_1[3]);
  Comparator #(.width(6)) comparator_2 (.a(in_1), .b(6'b000010), .eq(J));  // open: gt, lt
  and and_42 (Especial, and_41_out, in_1[2]);
  and and_43 (I, ~or_1_out, ~J);  // AND_Gate
  and and_44 (jr, ~in_2[0], R_00, in_2[3]);  // AND_Gate
  and and_45 (push, in_2[0], R_00, ~in_2[3]);  // AND_Gate
  and and_46 (and_46_out, ~in_2[0], R_00, ~in_2[3]);  // AND_Gate
  and and_47 (R, or_1_out, ~Especial);  // AND_Gate
  and and_48 (halt, in_2[0], Especial, in_2[1]);
  and and_49 (tty, in_2[0], Especial, ~in_2[1]);  // AND_Gate
  and and_50 (rnd, ~in_2[0], Especial, in_2[1]);  // AND_Gate
  and and_51 (kbd, ~in_2[0], Especial, ~in_2[1]);  // AND_Gate
  and and_52 (pop, and_46_out, in_1[5]);
  and and_53 (nop, and_46_out, ~in_1[5]);  // AND_Gate

  // Other names for the same wires on the sheet: F_bit1 = in_2[0]; FuncCode[5:0] = in_2; F_bit2 = in_2[1];
  //   F_bit3 = in_2[2]; F_bit4 = in_2[3]; MvHi = mfhi; MvLo = mflo; OpCode[5:0] = in_1; Bit3 = in_1[2];
  //   Bit4 = in_1[3]; Bit6 = in_1[5]
endmodule

module Type_AL (
  input  in_1,
  input  in_2,
  input  in_3,
  input  in_4,
  input  in_5,
  input  in_6,
  input  in_7,
  input  in_8,
  input  in_9,
  input  in_10,
  input  in_11,
  input  in_12,
  input  in_13,
  input  in_14,
  input  in_15,
  input  in_16,
  output RfRw,
  output Pc,
  output [1:0] BcSel,
  output [2:0] AluSel,
  output [2:0] DiSel,
  output HL
);

  wire not_1_out, or_4_out, or_5_out, or_6_out, or_7_out;
  wire [1:0] and_5_out;
  wire [2:0] or_1_out;

  or or_1 (or_1_out[0], in_8, in_10, in_2, in_4, in_12, in_6);
  or or_2 (or_1_out[1], in_6, in_7, in_8, in_11, in_12, in_5);
  or or_3 (or_1_out[2], in_9, in_11, in_10, in_12);
  or or_4 (or_4_out, in_3, in_4, in_5, in_6);
  and and_1 (HL, or_4_out, in_16);
  or or_5 (or_5_out, or_1_out[0], or_1_out[1], or_1_out[2]);
  assign AluSel = or_1_out & {3{in_16}};  // AND_Gate and_2, 3 bits wide
  or or_6 (or_6_out, in_1, or_5_out);
  or or_7 (or_7_out, or_6_out, in_13, in_14);
  not not_1 (not_1_out, in_13);
  and and_3 (RfRw, or_7_out, ~in_4, ~in_5, ~in_6, in_16);  // AND_Gate
  and and_4 (and_5_out[1], in_14, not_1_out);
  and and_5 (and_5_out[0], in_13, in_14);
  assign DiSel = {in_13, and_5_out} & {3{in_16}};  // AND_Gate and_6, 3 bits wide
  assign BcSel = {in_15, 1'b0} & {2{in_16}};  // AND_Gate and_7, 2 bits wide

  assign Pc = in_16;

  // Other names for the same wires on the sheet: MvHi = in_13; Enable = in_16; Jr = in_15; Add = in_1; And = in_7;
  //   Div = in_5; Divu = in_6; Mul = in_3; Mulu = in_4; MvLo = in_14; Nor = in_9; Or = in_8; Slt = in_11;
  //   Sltu = in_12; Sub = in_2; Xor = in_10
endmodule

module Type_H_L (
  input  in_1,
  input  in_2,
  input  in_3,
  input  in_4,
  output Wrf,
  output LdPc,
  output \end ,
  output [2:0] DiSel
);

  wire [1:1] not_1_out;

  not not_1 (not_1_out[1], in_1);
  D_Flip_Flop d_ff_1 (.clk(in_4), .D(in_3), .Q(\end ));  // open: Qn, preset, en, reset
  assign DiSel = {1'b0, not_1_out[1], in_1} & {3{in_3}};  // AND_Gate and_1, 3 bits wide

  assign LdPc = in_3;
  assign Wrf = in_3;

  // Other names for the same wires on the sheet: MvHi = in_1; Enable = in_3; Clk = in_4; MvLo = in_2
endmodule

module Type_Inmediate (
  input  in_1,
  input  in_2,
  input  in_3,
  input  in_4,
  input  in_5,
  input  in_6,
  input  in_7,
  output [2:0] AluSel,
  output [1:0] BSel,
  output DaSel,
  output Pc,
  output RwRf
);

  wire or_2_out, or_3_out;
  wire [0:0] or_1_out;
  wire [2:0] or_5_out;

  or or_1 (or_1_out[0], in_1, in_2, in_3, in_4, in_5, in_6);
  or or_2 (or_2_out, in_3, in_6);
  or or_3 (or_3_out, in_5, in_2);
  or or_4 (or_5_out[2], in_4, in_5, in_6);
  and and_1 (DaSel, or_1_out[0], in_7);
  or or_5 (or_5_out[0], in_4, or_2_out);
  or or_6 (or_5_out[1], or_2_out, or_3_out);
  assign BSel = {1'b0, or_1_out[0]} & {2{in_7}};  // AND_Gate and_2, 2 bits wide
  assign AluSel = or_5_out & {3{in_7}};  // AND_Gate and_3, 3 bits wide

  assign Pc = in_7;
  assign RwRf = in_7;

  // Other names for the same wires on the sheet: Enable = in_7; Addi = in_1; Andi = in_2; Ori = in_3; Slti = in_5;
  //   Sltiu = in_6; Xori = in_4
endmodule

module Type_Special (
  input  in_1,
  input  in_2,
  input  in_3,
  input  in_4,
  output EnableTty,
  output EnableKbd,
  output Pc,
  output [2:0] DiSel,
  output Rf
);

  wire [2:2] or_1_out;

  or or_1 (or_1_out[2], in_3, in_2);
  and and_1 (EnableTty, in_1, in_4);
  and and_2 (EnableKbd, in_3, in_4);
  and and_3 (Rf, or_1_out[2], in_4);
  assign DiSel = {{2{or_1_out[2]}}, in_3} & {3{in_4}};  // AND_Gate and_4, 3 bits wide

  assign Pc = in_4;

  // Other names for the same wires on the sheet: Kbd = in_3; Enable = in_4; Rnd = in_2; Tty = in_1
endmodule

module Type_Store_Word (
  input  in_1,
  input  in_2,
  input  in_3,
  output WriteRam,
  output [1:0] OperandBSelector,
  output EnRam,
  output LdPc,
  output End,
  output [1:0] AddrSel
);

  wire d_ff_1_q, demultiplexer_1_out0;

  D_Flip_Flop d_ff_1 (.clk(in_2), .D(demultiplexer_1_out0), .Q(d_ff_1_q));  // open: Qn, preset, en, reset
  or or_1 (AddrSel[0], in_1, d_ff_1_q);
  Demultiplexer #(.enable("false")) demultiplexer_1 (
    .out0(demultiplexer_1_out0), .out1(LdPc), .in(AddrSel[0]), .sel(in_3));
  D_Flip_Flop d_ff_2 (.clk(in_2), .D(LdPc), .Q(End));  // open: Qn, preset, en, reset

  assign AddrSel[1] = 1'b0;
  assign EnRam = in_1;
  assign OperandBSelector = {1'b0, AddrSel[0]};
  assign WriteRam = AddrSel[0];

  // Other names for the same wires on the sheet: AddrSel_t = AddrSel[0]; BSel = AddrSel[0]; BSelector[0] = AddrSel[0];
  //   RamW = AddrSel[0]; Clk = in_2; Enable = in_1; RamReady = in_3

  // Notes on the sheet:
  //   Inputs
  //   Outputs
endmodule

module Type_Load_Word (
  input  in_1,
  input  in_2,
  input  in_3,
  output [1:0] OperandBSelector,
  output EnRam,
  output Wrf,
  output LdPc,
  output End,
  output DaSel,
  output [2:0] DiSel,
  output [1:0] AddrSel
);

  wire d_ff_1_q, demultiplexer_1_out0;

  D_Flip_Flop d_ff_1 (.clk(in_2), .D(demultiplexer_1_out0), .Q(d_ff_1_q));  // open: Qn, preset, en, reset
  Demultiplexer #(.enable("false")) demultiplexer_1 (
    .out0(demultiplexer_1_out0), .out1(DaSel), .in(AddrSel[0]), .sel(in_3));
  or or_1 (AddrSel[0], d_ff_1_q, in_1);
  D_Flip_Flop d_ff_2 (.clk(in_2), .D(DaSel), .Q(End));  // open: Qn, preset, en, reset

  assign AddrSel[1] = 1'b0;
  assign DiSel = {2'b00, DaSel};
  assign EnRam = in_1;
  assign LdPc = DaSel;
  assign OperandBSelector = {1'b0, AddrSel[0]};
  assign Wrf = DaSel;

  // Other names for the same wires on the sheet: Clk = in_2; DiSel_t = DaSel; RfRw = DaSel; Enable = in_1;
  //   AddrSel_t = AddrSel[0]; BSel = AddrSel[0]; RamReady = in_3

  // Notes on the sheet:
  //   Inputs
  //   Outputs
endmodule

module Branch_Operations (
  input  in_1,
  input  in_2,
  input  in_3,
  input  in_4,
  input  in_5,
  input  in_6,
  input  in_7,
  input  in_8,
  output [2:0] FlagsSel,
  output [1:0] BcSel,
  output [2:0] AluSel,
  output Pc
);

  wire [0:0] or_4_out, or_5_out;
  wire [2:0] or_3_out;

  or or_1 (or_3_out[2], in_5, in_4);
  or or_2 (or_3_out[1], in_1, in_3);
  or or_3 (or_3_out[0], in_4, in_4);
  or or_4 (or_4_out[0], in_1, in_2, in_3, in_4, in_5);
  assign FlagsSel = or_3_out & {3{in_7}};  // AND_Gate and_1, 3 bits wide
  or or_5 (or_5_out[0], in_8, or_4_out[0]);
  assign AluSel = {2'b00, or_4_out[0]} & {3{in_7}};  // AND_Gate and_2, 3 bits wide
  assign BcSel = {2{in_7}} & {in_8, or_5_out[0]};  // AND_Gate and_3, 2 bits wide

  assign Pc = in_7;

  // Other names for the same wires on the sheet: Jmp = in_8; Enable = in_7; Beq = in_1; Bgtz = in_4; Blez = in_3;
  //   Bltz = in_5; Bne = in_2; Nop = in_6
endmodule

module Push (
  input  in_1,
  input  in_2,
  input  in_3,
  output ASel,
  output [1:0] BSel,
  output [1:0] AddrSel,
  output SpRw,
  output Pc,
  output [2:0] AluSel,
  output StartRam,
  output EndStack,
  output RamW,
  output DoSel
);

  wire d_ff_2_q, demultiplexer_1_out0;

  D_Flip_Flop d_ff_1 (.clk(in_3), .D(in_1), .Q(StartRam));  // open: Qn, preset, en, reset
  D_Flip_Flop d_ff_2 (.clk(in_3), .D(demultiplexer_1_out0), .Q(d_ff_2_q));  // open: Qn, preset, en, reset
  or or_1 (AddrSel[1], StartRam, d_ff_2_q);
  Demultiplexer #(.enable("false")) demultiplexer_1 (
    .out0(demultiplexer_1_out0), .out1(Pc), .in(AddrSel[1]), .sel(in_2));
  D_Flip_Flop d_ff_3 (.clk(in_3), .D(Pc), .Q(EndStack));  // open: Qn, preset, en, reset

  assign AddrSel[0] = AddrSel[1];
  assign AluSel = {2'b00, in_1};
  assign ASel = in_1;
  assign BSel = {2{in_1}};
  assign DoSel = AddrSel[1];
  assign RamW = AddrSel[1];
  assign SpRw = in_1;

  // Other names for the same wires on the sheet: AddrSel_t = AddrSel[1]; AluSel_t = in_1; BSel_t = in_1;
  //   Enable = in_1; Clk = in_3; EndPush = EndStack; RamReady = in_2
endmodule

module Pop (
  input  in_1,
  input  in_2,
  input  in_3,
  output Wrf,
  output EndStack,
  output ASel,
  output [1:0] BSel,
  output SpRw,
  output LdPc,
  output StartRam,
  output [2:0] DiSel,
  output [1:0] AddrSel
);

  wire d_ff_1_q, demultiplexer_1_out0;

  D_Flip_Flop d_ff_1 (.clk(in_3), .D(demultiplexer_1_out0), .Q(d_ff_1_q));  // open: Qn, preset, en, reset
  or or_1 (AddrSel[1], in_2, d_ff_1_q);
  Demultiplexer #(.enable("false")) demultiplexer_1 (
    .out0(demultiplexer_1_out0), .out1(ASel), .in(AddrSel[1]), .sel(in_1));
  D_Flip_Flop d_ff_2 (.clk(in_3), .D(ASel), .Q(EndStack));  // open: Qn, preset, en, reset

  assign AddrSel[0] = AddrSel[1];
  assign BSel = {2{ASel}};
  assign DiSel = {2'b00, ASel};
  assign LdPc = ASel;
  assign SpRw = ASel;
  assign StartRam = in_2;
  assign Wrf = ASel;

  // Other names for the same wires on the sheet: AddrSel_t = AddrSel[1]; Clk = in_3; BSel_t = ASel; DiSel_t = ASel;
  //   Pc = ASel; Enable = in_2; End = EndStack; RamReady = in_1
endmodule
